# Fritzing sketch RaspberryPi4(Final) (saved by Fritzing 1.0.5)

parts:
  Mod1 = Raspberry Pi 4B
  DHT1 = Humidity and Temperature Sensor DHT11
  Part1 = Barometric Pressure Sensor - BMP180 Breakout (GY-68)

nets:
  3V3: Mod1.3V3, DHT1.Vcc
  5V: Mod1.5V, Part1.VCC
  N1: Mod1.GPIO2, Part1.SDA
  N2: Mod1.GPIO3, Part1.SCL
  GND: Mod1.GND, DHT1.GND_2, Part1.GND
  N3: Mod1.GPIO22, DHT1.Data-signal

custom parts:
  Humidity and Temperature Sensor DHT11: Digital relative humidity & temperature sensor DHT11
